// Logisim project CRC_Module_all.circ as structural Verilog
module ModuloCRCALL (
  input  MD__selects_the_behaviour_of_the_chip,
  input  Line_IN,
  input  Clock,
  input  Reset,
  output Line_OUT,
  output BUSY
);

  wire md_enable_1_reg_in, Shift_Register_out, undriven;

  MD_Enable md_enable_1 (
    .MD(MD__selects_the_behaviour_of_the_chip), .LINE_IN(Line_IN), .REG_IN(md_enable_1_reg_in));  // open: CTRL_OUT
  Shift_Register Shift_Register (
    .in(md_enable_1_reg_in), .clk(Clock), .out(Shift_Register_out));  // open: shift, load, clr, d0, q0, d1, q1, d2, q2, d3, q3, d4, q4, d5, q5, d6, q6, d7, q7
  Multiplexer multiplexer_1 (.in0(Shift_Register_out), .out(Line_OUT), .sel(undriven));  // open: in1, en

  // Notes on the sheet:
  //   MD_Enable
endmodule

// do_xor
module Do_XOR (
  input  B,
  input  A,
  input  E,
  output C
);

  wire and_1_out;

  and and_1 (and_1_out, A, E);
  xor xor_1 (C, B, and_1_out);
endmodule

module MD_Enable (
  input  MD,
  input  CTRL_OUT,
  input  LINE_IN,
  output REG_IN
);

  wire or_1_out;

  or or_1 (or_1_out, MD, CTRL_OUT);
  and and_1 (REG_IN, or_1_out, LINE_IN);
endmodule

module CRC_Logic (
  input  in_1
);

  D_Flip_Flop d_ff_1 (.clk(in_1));  // open: D, Q, Qn, preset, en, reset
  D_Flip_Flop d_ff_2 (.clk(in_1));  // open: D, Q, Qn, preset, en, reset
  D_Flip_Flop d_ff_3 (.clk(in_1));  // open: D, Q, Qn, preset, en, reset
  D_Flip_Flop d_ff_4 (.clk(in_1));  // open: D, Q, Qn, preset, en, reset
  D_Flip_Flop d_ff_5 (.clk(in_1));  // open: D, Q, Qn, preset, en, reset
  D_Flip_Flop d_ff_6 (.clk(in_1));  // open: D, Q, Qn, preset, en, reset
  D_Flip_Flop d_ff_7 (.clk(in_1));  // open: D, Q, Qn, preset, en, reset
  D_Flip_Flop d_ff_8 (.clk(in_1));  // open: D, Q, Qn, preset, en, reset
endmodule
