// Logisim project CRC_Module_all.circ as structural Verilog: 5 circuits, main circuit ModuloCRCALL
module ModuloCRCALL (
  input  MD__selects_the_behaviour_of_the_chip,
  input  Line_IN,
  input  Clock,
  input  Reset,
  output Line_OUT,
  output BUSY
);

  wire crc_controller_1_q, crc_controller_1_u, md_enable_1_reg_in, Shift_Register_out, undriven;

  MD_Enable md_enable_1 (
    .MD(MD__selects_the_behaviour_of_the_chip), .CTRL_OUT(crc_controller_1_q), .LINE_IN(Line_IN),
    .REG_IN(md_enable_1_reg_in));
  CRC_Controller crc_controller_1 (.Clock(Clock), .Reset(Reset), .Q(crc_controller_1_q), .U(crc_controller_1_u));
  Shift_Register Shift_Register (
    .in(md_enable_1_reg_in), .clk(Clock), .out(Shift_Register_out));  // open: shift, load, clr, d0, q0, d1, q1, d2, q2, d3, q3, d4, q4, d5, q5, d6, q6, d7, q7
  Multiplexer multiplexer_1 (.in0(Shift_Register_out), .out(Line_OUT), .sel(undriven));  // open: in1, en

  // Notes on the sheet:
  //   MD_Enable
  //   enable_crc
endmodule

// do_xor
module Do_XOR (
  input  B,
  input  A,
  input  E,
  input  in_4,
  output C
);

  wire and_1_out;

  and and_1 (and_1_out, A, E);
  xor xor_1 (C, B, and_1_out);
endmodule

module MD_Enable (
  input  MD,
  input  CTRL_OUT,
  input  LINE_IN,
  output REG_IN
);

  wire or_1_out;

  or or_1 (or_1_out, MD, CTRL_OUT);
  and and_1 (REG_IN, or_1_out, LINE_IN);
endmodule

module CRC_Logic (
  input  Clock,
  input  CRC_IN,
  input  Enable_CRC,
  output CRC_OUT
);

  wire d_ff_1_q, d_ff_2_q, d_ff_3_q, d_ff_4_q, d_ff_5_q, d_ff_6_q, d_ff_7_q, undriven, x_0_c, x_2_c, x_4_c;

  Do_XOR x_0 (.B(CRC_IN), .A(CRC_OUT), .E(Enable_CRC), .C(x_0_c));  // open: in_4
  D_Flip_Flop d_ff_1 (.clk(Clock), .D(x_0_c), .Q(d_ff_1_q));  // open: Qn, preset, en, reset
  D_Flip_Flop d_ff_2 (.clk(Clock), .D(d_ff_1_q), .Q(d_ff_2_q));  // open: Qn, preset, en, reset
  Do_XOR x_2 (.B(d_ff_2_q), .A(CRC_OUT), .E(Enable_CRC), .C(x_2_c));  // open: in_4
  D_Flip_Flop d_ff_3 (
    .clk(Clock), .D(x_2_c), .Q(d_ff_3_q), .preset(undriven), .en(undriven), .reset(undriven));  // open: Qn
  D_Flip_Flop d_ff_4 (.clk(Clock), .D(d_ff_3_q), .Q(d_ff_4_q));  // open: Qn, preset, en, reset
  D_Flip_Flop d_ff_5 (.clk(Clock), .D(x_4_c), .Q(d_ff_5_q));  // open: Qn, preset, en, reset
  Do_XOR x_4 (.B(d_ff_4_q), .A(CRC_OUT), .E(Enable_CRC), .C(x_4_c));  // open: in_4
  D_Flip_Flop d_ff_6 (.clk(Clock), .D(d_ff_5_q), .Q(d_ff_6_q));  // open: Qn, preset, en, reset
  D_Flip_Flop d_ff_7 (.clk(Clock), .D(d_ff_6_q), .Q(d_ff_7_q));  // open: Qn, preset, en, reset
  D_Flip_Flop d_ff_8 (.clk(Clock), .D(d_ff_7_q), .Q(CRC_OUT));  // open: Qn, preset, en, reset
endmodule

// CRC Ctrl
module CRC_Controller (
  input  Clock,
  input  Reset,
  output Q,
  output U
);
endmodule
